// Digital circuit full-adder circuit.dig as structural Verilog
module full_adder_circuit (
  input  in_1,
  input  in_2,
  input  in_3,
  output out_4,
  output out_5
);

  Add add_1 (.a(in_1), .b(in_2), .c_i(in_3), .s(out_4), .c_o(out_5));
endmodule
