// Digital circuit fulladder.dig as structural Verilog
module fulladder (
  input  A_In,
  input  B_In,
  input  Carry_In,
  output Sum_Out,
  output Carry_Out
);

  Add add_1 (.a(A_In), .b(B_In), .c_i(Carry_In), .s(Sum_Out), .c_o(Carry_Out));
endmodule
