// Digital circuit half-adder circuit.dig as structural Verilog
module half_adder_circuit (
  input  A_In,
  input  B_In,
  output Sum_Out,
  output Carry_Out
);

  xor xor_1 (Sum_Out, A_In, B_In);
  and and_1 (Carry_Out, A_In, B_In);
endmodule
