// Digital circuit new8bitadder.dig as structural Verilog
module new8bitadder (
  input  [7:0] A_In,
  input  [7:0] B_In,
  input  Carry_In,
  output [7:0] Sum_Out,
  output Carry_Out
);

  wire fulladder_2_carry_out, fulladder_3_carry_out, fulladder_4_carry_out, fulladder_5_carry_out,
       fulladder_6_carry_out, fulladder_7_carry_out, fulladder_8_carry_out;

  fulladder fulladder_1 (
    .A_In(A_In[7]), .B_In(B_In[7]), .Carry_In(fulladder_2_carry_out), .Sum_Out(Sum_Out[7]),
    .Carry_Out(Carry_Out));
  fulladder fulladder_2 (
    .A_In(A_In[6]), .B_In(B_In[6]), .Carry_In(fulladder_3_carry_out), .Sum_Out(Sum_Out[6]),
    .Carry_Out(fulladder_2_carry_out));
  fulladder fulladder_3 (
    .A_In(A_In[5]), .B_In(B_In[5]), .Carry_In(fulladder_4_carry_out), .Sum_Out(Sum_Out[5]),
    .Carry_Out(fulladder_3_carry_out));
  fulladder fulladder_4 (
    .A_In(A_In[4]), .B_In(B_In[4]), .Carry_In(fulladder_5_carry_out), .Sum_Out(Sum_Out[4]),
    .Carry_Out(fulladder_4_carry_out));
  fulladder fulladder_5 (
    .A_In(A_In[3]), .B_In(B_In[3]), .Carry_In(fulladder_6_carry_out), .Sum_Out(Sum_Out[3]),
    .Carry_Out(fulladder_5_carry_out));
  fulladder fulladder_6 (
    .A_In(A_In[2]), .B_In(B_In[2]), .Carry_In(fulladder_7_carry_out), .Sum_Out(Sum_Out[2]),
    .Carry_Out(fulladder_6_carry_out));
  fulladder fulladder_7 (
    .A_In(A_In[1]), .B_In(B_In[1]), .Carry_In(fulladder_8_carry_out), .Sum_Out(Sum_Out[1]),
    .Carry_Out(fulladder_7_carry_out));
  fulladder fulladder_8 (
    .A_In(A_In[0]), .B_In(B_In[0]), .Carry_In(Carry_In), .Sum_Out(Sum_Out[0]),
    .Carry_Out(fulladder_8_carry_out));
endmodule
